// Logisim project Fluminense.circ as structural Verilog: 4 circuits, main circuit CPU
module CPU (
  input  Reset
);

  wire and_1_out, and_2_out, and_3_out, CLK_out, multiplexer_3_out, nor_1_out, not_1_out, not_2_out,
       or_1_out, setRegister_nf, setRegister_setregister, setRegister_zf, u_controle_1_imediato,
       u_controle_1_jump, u_controle_1_l___0___s___1, u_controle_1_mem___1_ula___0, u_controle_1_on,
       u_controle_1_setflag, u_controle_1_wb;
  wire [1:0] u_controle_1_jump_seletor;
  wire [15:0] adder_1_out, banco_de_registradores_1_reg1out, banco_de_registradores_1_reg2out,
       banco_de_registradores_1_regaout, banco_de_registradores_1_regbout, banco_de_registradores_1_regcout,
       banco_de_registradores_1_regdout, bit_extender_1_out, multiplexer_1_out, multiplexer_2_out,
       multiplexer_4_out, multiplexer_5_out, PC_q, ram_1_data, ram_2_data, setRegister_ula_output;

  Clock CLK (.out(CLK_out));
  Register #(.width(16)) PC (.D(multiplexer_1_out), .en(u_controle_1_on), .Q(PC_q), .clk(CLK_out), .clr(Reset));
  Adder #(.width(16)) adder_1 (.a(PC_q), .b(16'h1), .out(adder_1_out));  // open: cin, cout
  RAM #(.addrWidth(16), .dataWidth(16), .bus("separate")) ram_1 (
    .addr(PC_q), .data(ram_1_data), .ld(1'b1));  // open: din, str, sel, clk, clr
  Multiplexer #(.width(16), .enable("false")) multiplexer_1 (
    .in0(adder_1_out), .in1(multiplexer_4_out), .out(multiplexer_1_out), .sel(and_1_out));
  U_Controle u_controle_1 (
    .setFlag(u_controle_1_setflag), .WB(u_controle_1_wb), .Mem___1_ULA___0(u_controle_1_mem___1_ula___0),
    .L___0___S___1(u_controle_1_l___0___s___1), .\Instrução (ram_1_data), .Jump(u_controle_1_jump),
    .ON(u_controle_1_on), .Imediato(u_controle_1_imediato), .Jump_Seletor(u_controle_1_jump_seletor));
  // Probe on banco_de_registradores_1_regdout
  // Probe on banco_de_registradores_1_regcout
  // Probe on banco_de_registradores_1_regbout
  // Probe on banco_de_registradores_1_regaout
  assign bit_extender_1_out = {{8{ram_1_data[7]}}, ram_1_data[7:0]};  // Bit_Extender bit_extender_1
  and and_1 (and_1_out, multiplexer_3_out, u_controle_1_jump);
  Multiplexer #(.width(16), .enable("false")) multiplexer_2 (
    .in0(setRegister_ula_output), .in1(ram_2_data), .out(multiplexer_2_out),
    .sel(u_controle_1_mem___1_ula___0));
  and and_2 (and_2_out, or_1_out, ~CLK_out);  // AND_Gate
  Multiplexer #(.select(2), .enable("false")) multiplexer_3 (
    .in0(setRegister_zf), .in1(setRegister_nf), .in2(nor_1_out), .in3(1'b0), .out(multiplexer_3_out),
    .sel(u_controle_1_jump_seletor));
  Banco_de_Registradores banco_de_registradores_1 (
    .R_W(and_2_out), .NReg1_Dest(ram_1_data[11:10]), .DataIn(multiplexer_2_out),
    .Reg1Out(banco_de_registradores_1_reg1out), .NReg2(ram_1_data[9:8]),
    .Reg2Out(banco_de_registradores_1_reg2out), .RegAOut(banco_de_registradores_1_regaout),
    .RegBOut(banco_de_registradores_1_regbout), .RegCOut(banco_de_registradores_1_regcout),
    .RegDOut(banco_de_registradores_1_regdout), .CLK(CLK_out));  // open: CLR
  Multiplexer #(.width(16), .enable("false")) multiplexer_4 (
    .in0(banco_de_registradores_1_reg2out), .in1(bit_extender_1_out), .out(multiplexer_4_out),
    .sel(u_controle_1_imediato));
  LED ZF (.in(setRegister_zf));
  ULA setRegister (
    .Op1(banco_de_registradores_1_reg1out), .Op2(multiplexer_4_out), .clkIn(CLK_out), .WB(u_controle_1_wb),
    .setRegister(setRegister_setregister), .Seletor_OP(ram_1_data[15:12]), .setFlag(and_3_out),
    .ZF(setRegister_zf), .NF(setRegister_nf), .ULA_Output(setRegister_ula_output));
  LED NG (.in(setRegister_nf));
  nor nor_1 (nor_1_out, setRegister_zf, setRegister_nf);
  or or_1 (or_1_out, u_controle_1_mem___1_ula___0, setRegister_setregister);
  not not_1 (not_1_out, u_controle_1_l___0___s___1);
  and and_3 (and_3_out, and_2_out, u_controle_1_setflag);
  not not_2 (not_2_out, CLK_out);
  Multiplexer #(.width(16), .enable("false")) multiplexer_5 (
    .in0(banco_de_registradores_1_reg1out), .in1(banco_de_registradores_1_reg2out), .out(multiplexer_5_out),
    .sel(not_1_out));
  RAM #(.addrWidth(16), .dataWidth(16), .bus("separate")) ram_2 (
    .addr(multiplexer_5_out), .din(banco_de_registradores_1_reg2out), .data(ram_2_data),
    .str(u_controle_1_l___0___s___1), .clk(not_2_out), .ld(1'b1));  // open: sel, clr

  // Notes on the sheet:
  //   ON
  //   Endereço de Branch
  //   Memória de Instrução
  //   Instrução de Jump
  //   Imediato
  //   R/W
  //   ULA Out
  //   Memória OUT
  //   Instrução ULA
  //   PF
  //   WriteBack
  //   setFlags
  //   setFlag
  //   Clock
  //   Reg1
  //   Reg2
  //   load/store Instrução
  //   Memória de Dados
endmodule

module Banco_de_Registradores (
  input  R_W,
  input  [1:0] NReg1_Dest,
  input  [1:0] NReg2,
  input  [15:0] DataIn,
  input  CLR,
  input  CLK,
  output [15:0] RegAOut,
  output [15:0] RegBOut,
  output [15:0] RegCOut,
  output [15:0] RegDOut,
  output [15:0] Reg1Out,
  output [15:0] Reg2Out
);

  wire and_1_out, and_2_out, and_3_out, and_4_out, demultiplexer_1_out0, demultiplexer_1_out1,
       demultiplexer_1_out2, demultiplexer_1_out3;
  wire [15:0] register_1_q;

  Register #(.width(16), .trigger("falling")) register_1 (.D(DataIn), .Q(register_1_q), .clk(CLK));  // open: en, clr
  Demultiplexer #(.select(2), .enable("false")) demultiplexer_1 (
    .out0(demultiplexer_1_out0), .out1(demultiplexer_1_out1), .out2(demultiplexer_1_out2),
    .out3(demultiplexer_1_out3), .in(1'b1), .sel(NReg1_Dest));
  and and_1 (and_1_out, demultiplexer_1_out0, R_W);
  and and_2 (and_2_out, demultiplexer_1_out1, R_W);
  and and_3 (and_3_out, demultiplexer_1_out2, R_W);
  and and_4 (and_4_out, demultiplexer_1_out3, R_W);
  Register #(.width(16), .trigger("high")) RegAX (
    .D(register_1_q), .Q(RegAOut), .clk(and_1_out), .clr(CLR));  // open: en
  Register #(.width(16), .trigger("high")) RegBX (
    .D(register_1_q), .Q(RegBOut), .clk(and_2_out), .clr(CLR));  // open: en
  Register #(.width(16), .trigger("high")) RegCX (
    .D(register_1_q), .Q(RegCOut), .clk(and_3_out), .clr(CLR));  // open: en
  Register #(.width(16), .trigger("high")) RegDX (
    .D(register_1_q), .Q(RegDOut), .clk(and_4_out), .clr(CLR));  // open: en
  Multiplexer #(.select(2), .width(16), .enable("false")) multiplexer_1 (
    .in0(RegAOut), .in1(RegBOut), .in2(RegCOut), .in3(RegDOut), .out(Reg1Out), .sel(NReg1_Dest));
  Multiplexer #(.select(2), .width(16), .enable("false")) multiplexer_2 (
    .in0(RegAOut), .in1(RegBOut), .in2(RegCOut), .in3(RegDOut), .out(Reg2Out), .sel(NReg2));

  // Notes on the sheet:
  //   <--- just for Debug
endmodule

module U_Controle (
  input  [15:0] \Instrução ,
  output Imediato,
  output setFlag,
  output WB,
  output Jump,
  output [1:0] Jump_Seletor,
  output Mem___1_ULA___0,
  output L___0___S___1,
  output ON
);

  wire and_3_out, and_4_out, nand_1_out, nand_4_out, not_2_out, not_3_out;

  not not_1 (setFlag, \Instrução [15]);
  nand nand_1 (nand_1_out, ~\Instrução [13], \Instrução [14], \Instrução [15]);  // NAND_Gate
  and and_1 (Mem___1_ULA___0, ~\Instrução [12], \Instrução [13], ~\Instrução [14], \Instrução [15]);  // AND_Gate
  and and_2 (L___0___S___1, \Instrução [12], \Instrução [13], ~\Instrução [14], \Instrução [15]);  // AND_Gate
  nand nand_2 (ON, \Instrução [12], \Instrução [13], \Instrução [14], \Instrução [15]);
  nand nand_3 (Imediato, \Instrução [0], \Instrução [1], \Instrução [2], \Instrução [3], \Instrução [4], \Instrução [5], \Instrução [6], \Instrução [7]);
  and and_3 (and_3_out, nand_1_out, ~L___0___S___1);  // AND_Gate
  nand nand_4 (nand_4_out, ~\Instrução [12], \Instrução [13], \Instrução [14], \Instrução [15]);  // NAND_Gate
  and and_4 (and_4_out, and_3_out, nand_4_out);
  not not_2 (not_2_out, nand_1_out);
  not not_3 (not_3_out, nand_4_out);
  and and_5 (WB, and_4_out, ON);
  or or_1 (Jump, not_2_out, not_3_out);

  assign Jump_Seletor = \Instrução [13:12];
endmodule

module ULA (
  input  [15:0] Op1,
  input  [15:0] Op2,
  input  [3:0] Seletor_OP,
  input  clkIn,
  input  WB,
  input  setFlag,
  output [15:0] ULA_Output,
  output setRegister,
  output ZF,
  output NF
);

  wire nor_1_out, not_1_out;
  wire [15:0] adder_1_out, and_1_out, divider_1_out, multiplier_1_out, not_2_out, or_1_out, or_2_out,
       subtractor_1_out, xor_1_out;

  not not_1 (not_1_out, clkIn);
  assign or_1_out = Op1 | Op2;  // OR_Gate or_1, 16 bits wide
  assign not_2_out = ~Op1;  // NOT_Gate not_2, 16 bits wide
  assign and_1_out = Op1 & Op2;  // AND_Gate and_1, 16 bits wide
  assign xor_1_out = Op1 ^ Op2;  // XOR_Gate xor_1, 16 bits wide
  Adder #(.width(16)) adder_1 (.a(Op1), .b(Op2), .out(adder_1_out));  // open: cin, cout
  Subtractor #(.width(16)) subtractor_1 (.a(Op1), .b(Op2), .out(subtractor_1_out));  // open: bin, bout
  Multiplier #(.width(16)) multiplier_1 (.a(Op1), .b(Op2), .out(multiplier_1_out));  // open: cin, cout
  Divider #(.width(16)) divider_1 (.a(Op1), .b(Op2), .out(divider_1_out));  // open: upper, rem
  assign or_2_out = {16{1'b0}} | Op2;  // OR_Gate or_2, 16 bits wide
  and and_2 (setRegister, not_1_out, WB);
  Multiplexer #(.select(4), .width(16), .enable("false")) multiplexer_1 (
    .in0(or_1_out), .in1(not_2_out), .in2(and_1_out), .in3(xor_1_out), .in4(adder_1_out),
    .in5(subtractor_1_out), .in6(multiplier_1_out), .in7(divider_1_out), .in8(or_2_out), .in9(or_2_out),
    .in10({16{1'b0}}), .in11({16{1'b0}}), .in12({16{1'b0}}), .in13({16{1'b0}}), .in14({16{1'b0}}),
    .in15({16{1'b0}}), .out(ULA_Output), .sel(Seletor_OP));
  nor nor_1 (nor_1_out, ULA_Output[15], ULA_Output[14], ULA_Output[13], ULA_Output[12], ULA_Output[11], ULA_Output[10], ULA_Output[9], ULA_Output[8], ULA_Output[7], ULA_Output[6], ULA_Output[5], ULA_Output[4], ULA_Output[3], ULA_Output[2], ULA_Output[1], ULA_Output[0]);
  Register #(.width(1)) u_ZF (.D(nor_1_out), .Q(ZF), .clk(setFlag));  // open: en, clr
  Register #(.width(1)) u_NF (.D(ULA_Output[15]), .Q(NF), .clk(setFlag));  // open: en, clr

  // Notes on the sheet:
  //   8 - 9: MOV
endmodule
